// Digital circuit Circuito.dig as structural Verilog
module Circuito (
  input  B5,
  input  A5,
  input  B4,
  input  A4,
  input  B3,
  input  A3,
  input  B2,
  input  A2,
  input  B1,
  input  A1,
  input  B0,
  input  A0,
  input  _01,
  input  _00,
  output S0,
  output S1,
  output S2,
  output S4,
  output S6,
  output S3,
  output F,
  output S7,
  output S5
);

  wire F_MULT, F_SOMA, F_SUB, S0_COMP, S0_MULT, S0_SOMA, S0_SUB, S1_COMP, S1_MULT, S1_SOMA, S1_SUB, S2_COMP,
       S2_MULT, S2_SOMA, S2_SUB, S3_COMP, S3_MULT, S3_SOMA, S3_SUB, S4_COMP, S4_MULT, S4_SOMA, S4_SUB,
       S5_COMP, S5_MULT, S5_SOMA, S5_SUB, S6_MULT, S7_MULT;

  MultiplicacaoCircuito multiplicacaocircuito_1 (
    .B2(B2), .A2(A2), .A3(A3), .B3(B3), .A4(A4), .B4(B4), .B5(B5), .A5(A5), .B1(B1), .A1(A1), .B0(B0),
    .A0(A0), .S0(S0_MULT), .S1(S1_MULT), .S2(S2_MULT), .S3(S3_MULT), .S4(S4_MULT), .S5(S5_MULT),
    .S6(S6_MULT), .F(F_MULT), .S7(S7_MULT));
  ComparacaoCircuito comparacaocircuito_1 (
    .B5(B5), .A5(A5), .B4(B4), .A4(A4), .B3(B3), .A3(A3), .B2(B2), .A2(A2), .B1(B1), .A1(A1), .B0(B0),
    .A0(A0), .S0(S0_COMP), .S1(S1_COMP), .S2(S2_COMP), .S3(S3_COMP), .S4(S4_COMP), .S5(S5_COMP));
  SubtracaoCircuito subtracaocircuito_1 (
    .A5(A5), .A4(A4), .B3(B3), .A3(A3), .B2(B2), .A2(A2), .B1(B1), .A1(A1), .B0(B0), .A0(A0), .B4(B4),
    .B5(B5), .S0(S0_SUB), .S1(S1_SUB), .S2(S2_SUB), .S3(S3_SUB), .S4(S4_SUB), .F(F_SUB), .S5(S5_SUB));
  CircuitoDosMux circuitodosmux_1 (
    .S0_SUB(S0_SUB), .S0_SOMA(S0_SOMA), .O0(_00), .O1(_01), .S0_COMP(S0_COMP), .S0_MULT(S0_MULT),
    .S1_SUB(S1_SUB), .S1_SOMA(S1_SOMA), .S1_COMP(S1_COMP), .S1_MULT(S1_MULT), .S2_SUB(S2_SUB),
    .S2_SOMA(S2_SOMA), .S2_COMP(S2_COMP), .S2_MULT(S2_MULT), .S3_SUB(S3_SUB), .S3_SOMA(S3_SOMA),
    .S3_COMP(S3_COMP), .S3_MULT(S3_MULT), .S4_SUB(S4_SUB), .S4_SOMA(S4_SOMA), .S4_COMP(S4_COMP),
    .S4_MULT(S4_MULT), .S5_SUB(S5_SUB), .S5_SOMA(S5_SOMA), .S5_COMP(S5_COMP), .S5_MULT(S5_MULT),
    .S6_MULT(S6_MULT), .S7_MULT(S7_MULT), .F_MULT(F_MULT), .F_SOMA(F_SOMA), .F_SUB(F_SUB), .s5(S5), .s4(S4),
    .s3(S3), .s2(S2), .s1(S1), .s0(S0), .S6(S6), .S7(S7), .F(F));
  SomaCircuito somacircuito_1 (
    .B3(B3), .B2(B2), .B1(B1), .B0(B0), .A3(A3), .A2(A2), .A1(A1), .A0(A0), .A4(A4), .A5(A5), .B4(B4),
    .B5(B5), .s5(S5_SOMA), .s4(S4_SOMA), .s3(S3_SOMA), .s2(S2_SOMA), .s1(S1_SOMA), .s0(S0_SOMA), .F(F_SOMA));
endmodule
