// Digital circuit MultiplicacaoDigitos.dig as structural Verilog
module MultiplicacaoDigitos (
  input  B,
  input  A0,
  input  A1,
  input  A2,
  input  A3,
  output S0,
  output S1,
  output S2,
  output S3
);

  and and_1 (S0, B, A0);
  and and_2 (S1, B, A1);
  and and_3 (S2, B, A2);
  and and_4 (S3, B, A3);
endmodule
