// Digital circuit MuxDeF.dig as structural Verilog
module MuxDeF (
  input  O0,
  input  O1,
  input  SUB,
  input  SOMA,
  input  MULT,
  output F
);

  wire and_1_out, and_2_out, and_3_out, not_1_out, not_2_out, not_3_out, or_1_out;

  not not_1 (not_1_out, O1);
  not not_2 (not_2_out, O0);
  and and_1 (and_1_out, SOMA, not_1_out, not_2_out);
  not not_3 (not_3_out, O1);
  and and_2 (and_2_out, SUB, not_3_out, O0);
  and and_3 (and_3_out, MULT, O1, O0);
  or or_1 (or_1_out, and_2_out, and_3_out);
  or or_2 (F, and_1_out, or_1_out);
endmodule
