// Digital circuit SomaCircuito.dig as structural Verilog
module SomaCircuito (
  input  B3,
  input  B2,
  input  B1,
  input  B0,
  input  A3,
  input  A2,
  input  A1,
  input  A0,
  input  A4,
  input  A5,
  input  B4,
  input  B5,
  output s5,
  output s4,
  output s3,
  output s2,
  output s1,
  output s0,
  output F
);

  wire somadigito_1_co, somadigito_2_co, somadigito_3_co, somadigito_4_co, somadigito_5_co, somasemci_1_co;

  xor xor_1 (F, somadigito_1_co, somadigito_2_co);
  SomaDigito somadigito_1 (.A(A5), .B(B5), .Ci(somadigito_2_co), .S(s5), .Co(somadigito_1_co));
  SomaDigito somadigito_2 (.A(A4), .B(B4), .Ci(somadigito_3_co), .S(s4), .Co(somadigito_2_co));
  SomaDigito somadigito_3 (.A(A3), .B(B3), .Ci(somadigito_4_co), .S(s3), .Co(somadigito_3_co));
  SomaDigito somadigito_4 (.A(A2), .B(B2), .Ci(somadigito_5_co), .S(s2), .Co(somadigito_4_co));
  SomaDigito somadigito_5 (.A(A1), .B(B1), .Ci(somasemci_1_co), .S(s1), .Co(somadigito_5_co));
  SomaSemCi somasemci_1 (.A(A0), .B(B0), .S(s0), .Co(somasemci_1_co));
endmodule
