// Digital circuit SubtracaoCircuito.dig as structural Verilog
module SubtracaoCircuito (
  input  A5,
  input  A4,
  input  B3,
  input  A3,
  input  B2,
  input  A2,
  input  B1,
  input  A1,
  input  B0,
  input  A0,
  input  B4,
  input  B5,
  output S0,
  output S1,
  output S2,
  output S3,
  output S4,
  output F,
  output S5
);

  wire C0, C1, C2, C3, C4, C5, somadigito_1_co, somadigito_2_co, somadigito_3_co, somadigito_4_co,
       somadigito_5_co, somasemci_1_co;

  xor xor_1 (F, somadigito_1_co, somadigito_2_co);
  SomaDigito somadigito_1 (.A(A5), .B(C5), .Ci(somadigito_2_co), .S(S5), .Co(somadigito_1_co));
  SomaDigito somadigito_2 (.A(A4), .B(C4), .Ci(somadigito_3_co), .S(S4), .Co(somadigito_2_co));
  ComplementoDeDois complementodedois_1 (
    .B5(B5), .B4(B4), .B3(B3), .B2(B2), .B1(B1), .B0(B0), .C5(C5), .C4(C4), .C1(C1), .C0(C0), .C3(C3), .C2(C2));
  SomaDigito somadigito_3 (.A(A3), .B(C3), .Ci(somadigito_4_co), .S(S3), .Co(somadigito_3_co));
  SomaDigito somadigito_4 (.A(A2), .B(C2), .Ci(somadigito_5_co), .S(S2), .Co(somadigito_4_co));
  SomaDigito somadigito_5 (.A(A1), .B(C1), .Ci(somasemci_1_co), .S(S1), .Co(somadigito_5_co));
  SomaSemCi somasemci_1 (.A(A0), .B(C0), .S(S0), .Co(somasemci_1_co));
endmodule
