// Digital circuit CircuitoDosMux.dig as structural Verilog
module CircuitoDosMux (
  input  S0_SUB,
  input  S0_SOMA,
  input  O0,
  input  O1,
  input  S0_COMP,
  input  S0_MULT,
  input  S1_SUB,
  input  S1_SOMA,
  input  S1_COMP,
  input  S1_MULT,
  input  S2_SUB,
  input  S2_SOMA,
  input  S2_COMP,
  input  S2_MULT,
  input  S3_SUB,
  input  S3_SOMA,
  input  S3_COMP,
  input  S3_MULT,
  input  S4_SUB,
  input  S4_SOMA,
  input  S4_COMP,
  input  S4_MULT,
  input  S5_SUB,
  input  S5_SOMA,
  input  S5_COMP,
  input  S5_MULT,
  input  S6_MULT,
  input  S7_MULT,
  input  F_MULT,
  input  F_SOMA,
  input  F_SUB,
  output s5,
  output s4,
  output s3,
  output s2,
  output s1,
  output s0,
  output S6,
  output S7,
  output F
);

  DigitosMux digitosmux_1 (.Soma(S0_SOMA), .Comp(S0_COMP), .Sub(S0_SUB), .Mult(S0_MULT), .O0(O0), .O1(O1), .S(s0));
  DigitosMux digitosmux_2 (.Soma(S1_SOMA), .Comp(S1_COMP), .Sub(S1_SUB), .Mult(S1_MULT), .O0(O0), .O1(O1), .S(s1));
  DigitosMux digitosmux_3 (.Soma(S2_SOMA), .Comp(S2_COMP), .Sub(S2_SUB), .Mult(S2_MULT), .O0(O0), .O1(O1), .S(s2));
  DigitosMux digitosmux_4 (.Soma(S3_SOMA), .Comp(S3_COMP), .Sub(S3_SUB), .Mult(S3_MULT), .O0(O0), .O1(O1), .S(s3));
  BitsExtraDaMultMux bitsextradamultmux_1 (.O0(O0), .O1(O1), .S_MULT(S6_MULT), .S(S6));
  DigitosMux digitosmux_5 (.Soma(S4_SOMA), .Comp(S4_COMP), .Sub(S4_SUB), .Mult(S4_MULT), .O0(O0), .O1(O1), .S(s4));
  DigitosMux digitosmux_6 (.Soma(S5_SOMA), .Comp(S5_COMP), .Sub(S5_SUB), .Mult(S5_MULT), .O0(O0), .O1(O1), .S(s5));
  BitsExtraDaMultMux bitsextradamultmux_2 (.O0(O0), .O1(O1), .S_MULT(S7_MULT), .S(S7));
  MuxDeF muxdef_1 (.O0(O0), .O1(O1), .SUB(F_SUB), .SOMA(F_SOMA), .MULT(F_MULT), .F(F));
endmodule
