// Digital circuit ComparacaoCircuito.dig as structural Verilog
module ComparacaoCircuito (
  input  B5,
  input  A5,
  input  B4,
  input  A4,
  input  B3,
  input  A3,
  input  B2,
  input  A2,
  input  B1,
  input  A1,
  input  B0,
  input  A0,
  output S0,
  output S1,
  output S2,
  output S3,
  output S4,
  output S5
);

  wire and_2_out, and_3_out, and_4_out, and_6_out, not_1_out, not_2_out, not_3_out, not_4_out, not_5_out,
       not_6_out, not_7_out, xor_1_out, xor_2_out, xor_3_out, xor_4_out, xor_5_out, xor_6_out;

  not not_1 (not_1_out, not_2_out);
  and and_1 (S1, not_2_out, not_1_out);
  xor xor_1 (xor_1_out, A5, B5);
  not not_2 (not_2_out, xor_1_out);
  not not_3 (not_3_out, xor_2_out);
  and and_2 (and_2_out, not_3_out, not_2_out);
  xor xor_2 (xor_2_out, A4, B4);
  and and_3 (and_3_out, and_4_out, and_2_out);
  xor xor_3 (xor_3_out, A3, B3);
  not not_4 (not_4_out, xor_3_out);
  not not_5 (not_5_out, xor_4_out);
  and and_4 (and_4_out, not_5_out, not_4_out);
  and and_5 (S0, and_6_out, and_3_out);
  xor xor_4 (xor_4_out, A2, B2);
  xor xor_5 (xor_5_out, A1, B1);
  not not_6 (not_6_out, xor_5_out);
  not not_7 (not_7_out, xor_6_out);
  and and_6 (and_6_out, not_7_out, not_6_out);
  xor xor_6 (xor_6_out, A0, B0);

  assign S2 = S1;
  assign S3 = S1;
  assign S4 = S1;
  assign S5 = S1;
endmodule
