// Digital circuit ComplementoDeDois.dig as structural Verilog
module ComplementoDeDois (
  input  B5,
  input  B4,
  input  B3,
  input  B2,
  input  B1,
  input  B0,
  output C5,
  output C4,
  output C1,
  output C0,
  output C3,
  output C2
);

  wire not_1_out, not_2_out, not_3_out, not_4_out, not_5_out, not_6_out, not_7_out, or_1_out, somasemci_2_co,
       somasemci_3_co, somasemci_4_co, somasemci_5_co, somasemci_6_co;

  not not_1 (not_1_out, B5);
  SomaSemCi somasemci_1 (.A(somasemci_2_co), .B(not_1_out), .S(C5));  // open: Co
  not not_2 (not_2_out, B4);
  SomaSemCi somasemci_2 (.A(somasemci_3_co), .B(not_2_out), .S(C4), .Co(somasemci_2_co));
  not not_3 (not_3_out, B3);
  SomaSemCi somasemci_3 (.A(somasemci_4_co), .B(not_3_out), .S(C3), .Co(somasemci_3_co));
  not not_4 (not_4_out, B2);
  SomaSemCi somasemci_4 (.A(somasemci_5_co), .B(not_4_out), .S(C2), .Co(somasemci_4_co));
  not not_5 (not_5_out, B1);
  SomaSemCi somasemci_5 (.A(somasemci_6_co), .B(not_5_out), .S(C1), .Co(somasemci_5_co));
  not not_6 (not_6_out, B0);
  SomaSemCi somasemci_6 (.A(or_1_out), .B(not_6_out), .S(C0), .Co(somasemci_6_co));
  not not_7 (not_7_out, B0);
  or or_1 (or_1_out, B0, not_7_out);
endmodule
