// Digital circuit MultiplicacaoCircuito.dig as structural Verilog
module MultiplicacaoCircuito (
  input  B2,
  input  A2,
  input  A3,
  input  B3,
  input  A4,
  input  B4,
  input  B5,
  input  A5,
  input  B1,
  input  A1,
  input  B0,
  input  A0,
  output S0,
  output S1,
  output S2,
  output S3,
  output S4,
  output S5,
  output S6,
  output F,
  output S7
);

  wire B0_A1, B0_A2, B0_A3, B1_A0, B1_A1, B1_A2, B1_A3, B2_A0, B2_A1, B2_A2, B2_A3, B3_A0, B3_A1, B3_A2,
       B3_A3, or_1_out, or_2_out, somadigito_1_co, somadigito_1_s, somadigito_2_co, somadigito_2_s,
       somadigito_3_co, somadigito_3_s, somadigito_4_co, somadigito_4_s, somadigito_5_co, somadigito_5_s,
       somadigito_6_co, somadigito_6_s, somasemci_1_co, somasemci_2_co, somasemci_3_co, somasemci_4_co,
       somasemci_4_s, somasemci_5_co, somasemci_5_s, somasemci_6_co, somasemci_7_co, somasemci_7_s,
       somasemci_8_co, somasemci_9_s, somasemci_10_co;

  or or_1 (or_1_out, A4, B4);
  or or_2 (or_2_out, A5, B5);
  or or_3 (F, or_1_out, or_2_out);
  MultiplicacaoDigitos multiplicacaodigitos_1 (
    .B(B0), .A0(A0), .A1(A1), .A2(A2), .A3(A3), .S0(S0), .S1(B0_A1), .S2(B0_A2), .S3(B0_A3));
  MultiplicacaoDigitos multiplicacaodigitos_2 (
    .B(B1), .A0(A0), .A1(A1), .A2(A2), .A3(A3), .S0(B1_A0), .S1(B1_A1), .S2(B1_A2), .S3(B1_A3));
  MultiplicacaoDigitos multiplicacaodigitos_3 (
    .B(B2), .A0(A0), .A1(A1), .A2(A2), .A3(A3), .S0(B2_A0), .S1(B2_A1), .S2(B2_A2), .S3(B2_A3));
  MultiplicacaoDigitos multiplicacaodigitos_4 (
    .B(B3), .A0(A0), .A1(A1), .A2(A2), .A3(A3), .S0(B3_A0), .S1(B3_A1), .S2(B3_A2), .S3(B3_A3));
  SomaSemCi somasemci_1 (.A(B0_A1), .B(B1_A0), .S(S1), .Co(somasemci_1_co));
  SomaDigito somadigito_1 (.A(B0_A2), .B(B1_A1), .Ci(somasemci_1_co), .S(somadigito_1_s), .Co(somadigito_1_co));
  SomaSemCi somasemci_2 (.A(somadigito_1_s), .B(B2_A0), .S(S2), .Co(somasemci_2_co));
  SomaDigito somadigito_2 (.A(B0_A3), .B(B1_A2), .Ci(somadigito_1_co), .S(somadigito_2_s), .Co(somadigito_2_co));
  SomaDigito somadigito_3 (.A(B1_A3), .B(B2_A2), .Ci(somadigito_2_co), .S(somadigito_3_s), .Co(somadigito_3_co));
  SomaDigito somadigito_4 (
    .A(somadigito_2_s), .B(B2_A1), .Ci(somasemci_2_co), .S(somadigito_4_s), .Co(somadigito_4_co));
  SomaDigito somadigito_5 (.A(B2_A3), .B(B3_A2), .Ci(somadigito_3_co), .S(somadigito_5_s), .Co(somadigito_5_co));
  SomaSemCi somasemci_3 (.A(somadigito_4_s), .B(B3_A0), .S(S3), .Co(somasemci_3_co));
  SomaDigito somadigito_6 (
    .A(somadigito_3_s), .B(B3_A1), .Ci(somadigito_4_co), .S(somadigito_6_s), .Co(somadigito_6_co));
  SomaSemCi somasemci_4 (.A(somadigito_5_s), .B(somadigito_6_co), .S(somasemci_4_s), .Co(somasemci_4_co));
  SomaSemCi somasemci_5 (.A(B3_A3), .B(somadigito_5_co), .S(somasemci_5_s), .Co(somasemci_5_co));
  SomaSemCi somasemci_6 (.A(somadigito_6_s), .B(somasemci_3_co), .S(S4), .Co(somasemci_6_co));
  SomaSemCi somasemci_7 (.A(somasemci_5_s), .B(somasemci_4_co), .S(somasemci_7_s), .Co(somasemci_7_co));
  SomaSemCi somasemci_8 (.A(somasemci_4_s), .B(somasemci_6_co), .S(S5), .Co(somasemci_8_co));
  SomaSemCi somasemci_9 (.A(somasemci_7_co), .B(somasemci_5_co), .S(somasemci_9_s));  // open: Co
  SomaSemCi somasemci_10 (.A(somasemci_7_s), .B(somasemci_8_co), .S(S6), .Co(somasemci_10_co));
  SomaSemCi somasemci_11 (.A(somasemci_9_s), .B(somasemci_10_co), .S(S7));  // open: Co
endmodule
