// Digital circuit SomaDigito.dig as structural Verilog
module SomaDigito (
  input  A,
  input  B,
  input  Ci,
  output S,
  output Co
);

  wire and_1_out, and_2_out, and_3_out, or_1_out, xor_1_out;

  xor xor_1 (xor_1_out, A, B);
  and and_1 (and_1_out, Ci, B);
  and and_2 (and_2_out, Ci, A);
  and and_3 (and_3_out, B, A);
  or or_1 (or_1_out, and_1_out, and_2_out);
  xor xor_2 (S, xor_1_out, Ci);
  or or_2 (Co, or_1_out, and_3_out);
endmodule
