// Digital circuit main.dig as structural Verilog
module main (
  input  B3,
  input  B2,
  input  B1,
  input  B0,
  input  O0,
  input  A3,
  input  A2,
  input  A1,
  input  A0,
  input  O1,
  input  A4,
  input  A5,
  input  B4,
  input  B5,
  output F,
  output s7,
  output s6,
  output s5,
  output s4,
  output s3,
  output s2,
  output s1,
  output s0
);

  Circuito circuito_1 (
    .B5(B5), .B4(B4), .B3(B3), .B2(B2), .B1(B1), .B0(B0), ._01(O1), ._00(O0), .A5(A5), .A4(A4), .A3(A3),
    .A2(A2), .A1(A1), .A0(A0), .F(F), .S7(s7), .S6(s6), .S5(s5), .S4(s4), .S3(s3), .S2(s2), .S1(s1), .S0(s0));
endmodule
