// Digital circuit Digito0.dig as structural Verilog
module Digito0 (
  input  B,
  input  S1,
  input  S2,
  input  S0_2,
  output S0
);

  wire and_1_out, and_2_out, and_3_out, not_1_out, not_2_out, not_3_out, not_4_out, not_5_out;

  not not_1 (not_1_out, S0_2);
  and and_1 (and_1_out, B, not_1_out);
  not not_2 (not_2_out, S1);
  not not_3 (not_3_out, S0_2);
  and and_2 (and_2_out, not_3_out, not_2_out, S2);
  or or_1 (S0, and_3_out, and_2_out, and_1_out);
  not not_4 (not_4_out, S2);
  not not_5 (not_5_out, S0_2);
  and and_3 (and_3_out, not_5_out, S1, not_4_out);
endmodule
