// Digital circuit Digito2.dig as structural Verilog
module Digito2 (
  input  S0,
  input  B,
  input  S1,
  input  S2,
  output S2_2
);

  wire and_1_out, and_2_out, and_3_out, and_4_out, not_1_out, not_2_out, not_3_out, not_4_out;

  and and_1 (and_1_out, S2, S1, B);
  not not_1 (not_1_out, S2);
  and and_2 (and_2_out, S0, S1, not_1_out);
  or or_1 (S2_2, and_4_out, and_3_out, and_2_out, and_1_out);
  not not_2 (not_2_out, S0);
  not not_3 (not_3_out, S1);
  and and_3 (and_3_out, not_2_out, not_3_out, S2);
  not not_4 (not_4_out, S2);
  and and_4 (and_4_out, not_4_out, B, S0);
endmodule
