// Digital circuit Seta.dig as structural Verilog
module Seta (
  input  clk
);

  wire Botao_Seta_Direita_out, Botao_Seta_Esquerda_out, resposta_1_l, resposta_2_l;

  LED Seta_Esquerda (.in(resposta_1_l));
  resposta resposta_1 (.clock(clk), .B(Botao_Seta_Esquerda_out), .L(resposta_1_l));
  DipSwitch Botao_Seta_Esquerda (.out(Botao_Seta_Esquerda_out));
  DipSwitch Botao_Seta_Direita (.out(Botao_Seta_Direita_out));
  resposta resposta_2 (.clock(clk), .B(Botao_Seta_Direita_out), .L(resposta_2_l));
  LED Seta_Direita (.in(resposta_2_l));
endmodule
