// Digital circuit resposta.dig as structural Verilog
module resposta (
  input  clock,
  input  B,
  output L
);

  wire d_ff_1_q, d_ff_2_q, digito0_1_s0, digito1_1_s1_2, digito2_1_s2_2, rs_ff_as_1_q;

  RS_FF_AS rs_ff_as_1 (.S(B), .R(clock), .Q(rs_ff_as_1_q));  // open: nQ
  Digito2 digito2_1 (.S0(L), .B(rs_ff_as_1_q), .S1(d_ff_2_q), .S2(d_ff_1_q), .S2_2(digito2_1_s2_2));
  D_FF d_ff_1 (.D(digito2_1_s2_2), .C(clock), .Q(d_ff_1_q));  // open: nQ
  D_FF d_ff_2 (.D(digito1_1_s1_2), .C(clock), .Q(d_ff_2_q));  // open: nQ
  Digito1 digito1_1 (.S0(L), .B(rs_ff_as_1_q), .S1(d_ff_2_q), .S2(d_ff_1_q), .S1_2(digito1_1_s1_2));
  D_FF d_ff_3 (.D(digito0_1_s0), .C(clock), .Q(L));  // open: nQ
  Digito0 digito0_1 (.B(rs_ff_as_1_q), .S1(d_ff_2_q), .S2(d_ff_1_q), .S0_2(L), .S0(digito0_1_s0));
endmodule
